# Fritzing sketch DIY_makey_Micro_BB_2Keys (saved by Fritzing 0.9.10b)
breadboards: 1

parts:
  Part1 = Arduino Micro (Rev3)  # not connected
  R16 = Resistor [tolerance=±5% resistance=10M package="0603 [SMD]"]  # not connected
  R20 = Resistor [tolerance=±5% resistance=10M package="0603 [SMD]"]
  R21 = Resistor [tolerance=±5% resistance=10M package="0603 [SMD]"]

nets:
  N1: R20.Pin_0, R21.Pin_0

notes:
  w
  a
  Ground connections
