# Fritzing sketch DIY_makey_Micro_BB_Complete (saved by Fritzing 0.9.10b)
breadboards: 1

parts:
  Part1 = Arduino Micro (Rev3)  # not connected
  R3 = Resistor [tolerance=±5% resistance=10M package="0603 [SMD]"]
  R10 = Resistor [tolerance=±5% resistance=10M package="0603 [SMD]"]
  R11 = Resistor [tolerance=±5% resistance=10M package="0603 [SMD]"]
  R12 = Resistor [tolerance=±5% resistance=10M package="0603 [SMD]"]
  R13 = Resistor [tolerance=±5% resistance=10M package="0603 [SMD]"]
  R14 = Resistor [tolerance=±5% resistance=10M package="0603 [SMD]"]
  R15 = Resistor [tolerance=±5% resistance=10M package="0603 [SMD]"]
  R16 = Resistor [tolerance=±5% resistance=10M package="0603 [SMD]"]  # not connected
  R17 = Resistor [tolerance=±5% resistance=10M package="0603 [SMD]"]
  R18 = Resistor [tolerance=±5% resistance=10M package="0603 [SMD]"]
  R19 = Resistor [tolerance=±5% resistance=10M package="0603 [SMD]"]
  R20 = Resistor [tolerance=±5% resistance=10M package="0603 [SMD]"]
  R21 = Resistor [tolerance=±5% resistance=10M package="0603 [SMD]"]

nets:
  N1: R3.Pin_0, R10.Pin_0, R11.Pin_0, R12.Pin_0, R13.Pin_0, R14.Pin_0, R15.Pin_0, R17.Pin_0, R18.Pin_0, R19.Pin_0, R20.Pin_0, R21.Pin_0

notes:
  w
  a
  x
  e
  ↓
  →
  ↑
  ←
  space
  d
  q
  s
  Ground connections
